# Fritzing sketch AKI (saved by Fritzing 0.9.10b)
breadboards: 1

parts:
  AKI = Arduino Uno (Rev3)
  R1 = Resistor [tolerance=±5% power=0.25 resistance=330 package=THT]
  R2 = Resistor [tolerance=±5% power=0.25 resistance=330 package=THT]
  LED5 = smd LED [color="White (4500K)" package="0805 [SMD]"]
  R4 = Resistor [tolerance=±5% power=0.25 resistance=330 package=THT]
  LED6 = smd LED [color="Red (633nm)" package="0805 [SMD]"]
  LED7 = smd LED [color="Red (633nm)" package="0805 [SMD]"]
  S1 = Pushbutton [package="[THT]"]
  R5 = Resistor [tolerance=±5% power=0.25 resistance=10k package=THT]

nets:
  N1: AKI.D10_PWM/SS, LED6.anode
  N2: AKI.D11_PWM/MOSI, LED7.anode
  N3: AKI.GND, R1.Pin_1, R2.Pin_1, R4.Pin_1, R5.Pin_1
  N4: AKI.D5_PWM, S1.Pin_3, S1.Pin_4, R5.Pin_0
  N5: AKI.D6_PWM, LED5.anode
  N6: AKI.5V, S1.Pin_1, S1.Pin_2
  N7: R1.Pin_0, LED7.cathode
  N8: R2.Pin_0, LED6.cathode
  N9: LED5.cathode, R4.Pin_0
