# Fritzing sketch preemptive (saved by Fritzing 0.9.10b)
breadboards: 1

parts:
  Knipperlicht = Arduino Uno (Rev3)
  R1 = Resistor [tolerance=±5% power=0.25 resistance=330 package=THT]
  R2 = Resistor [tolerance=±5% power=0.25 resistance=330 package=THT]
  LED4 = smd LED [color="Red (633nm)" package="0805 [SMD]"]
  R3 = Resistor [tolerance=±5% power=0.25 resistance=330 package=THT]
  LED5 = smd LED [color="Red (633nm)" package="0805 [SMD]"]
  R4 = Resistor [tolerance=±5% power=0.25 resistance=330 package=THT]
  LED6 = smd LED [color="Red (633nm)" package="0805 [SMD]"]
  LED7 = smd LED [color="Red (633nm)" package="0805 [SMD]"]

nets:
  N1: Knipperlicht.D10_PWM/SS, LED6.anode
  N2: Knipperlicht.D11_PWM/MOSI, LED7.anode
  N3: Knipperlicht.GND, R1.Pin_1, R2.Pin_1, R3.Pin_1, R4.Pin_1
  N4: Knipperlicht.D5_PWM, LED4.anode
  N5: Knipperlicht.D6_PWM, LED5.anode
  N6: R1.Pin_0, LED7.cathode
  N7: R2.Pin_0, LED6.cathode
  N8: LED4.cathode, R3.Pin_0
  N9: LED5.cathode, R4.Pin_0
