# Fritzing sketch CDebounce (saved by Fritzing 0.9.10b)
breadboards: 1

parts:
  AKI = Arduino Uno (Rev3)
  LED5 = smd LED [color="Red (633nm)" current=0A package="0805 [SMD]"]
  S1 = Pushbutton [package="[THT]"]
  R4 = Resistor [tolerance=±5% power=0.25 resistance=330 package=THT]
  R5 = Resistor [tolerance=±5% power=0.25 resistance=330 package=THT]

nets:
  N1: AKI.D11_PWM/MOSI, R4.Pin_1
  N2: AKI.GND, LED5.anode, R5.Pin_0
  N3: AKI.D7, S1.Pin_1, S1.Pin_2, R5.Pin_1
  N4: AKI.5V, S1.Pin_3, S1.Pin_4
  N5: LED5.cathode, R4.Pin_0
